# Fritzing sketch circuit (saved by Fritzing 0.9.1b)
circuit board: 8.46667cm x 5.64444cm
breadboards: 1

parts:
  U1 = atmega328 [package=dip]
  U2 = microSD Socket [package="Molex 502774-0891 [SMD]"]
  C1 = Ceramic Capacitor [capacitance="100 nF" package="0603 [SMD, multilayer]"]
  C2 = Ceramic Capacitor [capacitance=22pF package="0603 [SMD, multilayer]"]
  C3 = Ceramic Capacitor [capacitance=22pF package="0603 [SMD, multilayer]"]
  XTAL2 = Crystal [frequency="16 Mhz" package=THT]
  LED2 = smd LED [color="Red (633nm)" package="1206 [SMD]"]
  R1 = Resistor [tolerance=±20% resistance=220 package=THT]
  R2 = Resistor [tolerance=±5% resistance=220 package=THT]
  IC1 = Switching step-up voltage regulator [package=sot23-5]
  J1 = Infrared Proximity Sensor
  JP2 = Header 6 [package=1x06_smd_straight_alt]
  R3 = Resistor [tolerance=±20% resistance=50 package=THT]

nets:
  N1: U1.RESET, C1.1, R1.Pin_1
  N2: U1.D0_(RX), JP2.3
  N3: U1.D1_(TX), JP2.2
  VCC: U1.VCC, U2.VCC, R1.Pin_0, IC1.OUT, JP2.5
  GND: U1.GND, U1.A5, U2.DI, C2.0, C3.0, R2.Pin_0, IC1.GND, J1.GND, JP2.6, R3.Pin_0
  N4: U1.XLAT1, C2.1, XTAL2.pin_0
  N5: U1.XLAT2, C3.1, XTAL2.pin_1
  N6: U1.D7, J1.Vcc
  N7: U1.D8, LED2.anode
  N8: U1.D10_(PWM), U2.NC
  N9: U1.D11_(PWM), U2.CS
  N10: U1.D12, U2.DO
  N11: U1.D13, U2.SCK
  N12: U1.A4, J1.Vout
  N13: C1.0, JP2.1
  N14: LED2.cathode, R2.Pin_1
  N15: IC1.LX, JP2.4, R3.Pin_1
